// Logisim project Calc.circ as structural Verilog: 7 circuits, main circuit Calculator
module Calculator (
  input  A_sign,
  input  A1,
  input  A0,
  input  OPERATION,
  input  in_5,
  input  B_sign,
  input  B1,
  input  B0
);

  wire ADDER___SUBTERACTOR_out_9, ADDER___SUBTERACTOR_out_10, ADDER___SUBTERACTOR_out_11,
       ADDER___SUBTERACTOR_out_12, and_1_out, and_2_out, and_3_out, and_4_out, decoder_1_a_2, decoder_1_b_2,
       decoder_1_c_2, decoder_1_d_2, decoder_1_e, decoder_1_f, decoder_1_g, multiplexer_1_out,
       multiplexer_2_out, multiplexer_3_out, multiplexer_4_out, MULTIPLICATION_f1, MULTIPLICATION_f2,
       MULTIPLICATION_f3, MULTIPLICATION_f4, MULTIPLICATION_sign_f, not_1_out, not_2_out, not_3_out,
       or_1_out, REMAINDER_div_zero_flag, REMAINDER_f0, REMAINDER_f1, REMAINDER_sign_f;

  Multiplication MULTIPLICATION (
    .Sign_B(B_sign), .B1(B1), .B0(B0), .Sign_A(A_sign), .B1_2(A1), .B0_2(A0), .Sign_F(MULTIPLICATION_sign_f),
    .F1(MULTIPLICATION_f1), .F2(MULTIPLICATION_f2), .F3(MULTIPLICATION_f3), .F4(MULTIPLICATION_f4));
  Remainder REMAINDER (
    .Sign_A(A_sign), .A0(A0), .A1(A1), .Sign_B(B_sign), .B0(B0), .B1(B1), .Sign_F(REMAINDER_sign_f),
    .F0(REMAINDER_f0), .F1(REMAINDER_f1), .Div_Zero_Flag(REMAINDER_div_zero_flag));
  Add___Sub ADDER___SUBTERACTOR (
    .A_sign(A_sign), .A1(A1), .A0(A0), .OPERATION(OPERATION), .in_5(in_5), .B_sign(B_sign), .B1(B1), .B0(B0),
    .out_9(ADDER___SUBTERACTOR_out_9), .out_10(ADDER___SUBTERACTOR_out_10),
    .out_11(ADDER___SUBTERACTOR_out_11), .out_12(ADDER___SUBTERACTOR_out_12));
  Multiplexer #(.select(2), .enable("false")) multiplexer_1 (
    .in0(ADDER___SUBTERACTOR_out_12), .in1(ADDER___SUBTERACTOR_out_12), .in2(MULTIPLICATION_f4),
    .in3(REMAINDER_f0), .out(multiplexer_1_out), .sel({OPERATION, in_5}));
  Multiplexer #(.select(2), .enable("false")) multiplexer_2 (
    .in0(ADDER___SUBTERACTOR_out_10), .in1(ADDER___SUBTERACTOR_out_10), .in2(MULTIPLICATION_f2), .in3(1'b0),
    .out(multiplexer_2_out), .sel({OPERATION, in_5}));
  Multiplexer #(.select(2), .enable("false")) multiplexer_3 (
    .in0(ADDER___SUBTERACTOR_out_11), .in1(ADDER___SUBTERACTOR_out_11), .in2(MULTIPLICATION_f3),
    .in3(REMAINDER_f1), .out(multiplexer_3_out), .sel({OPERATION, in_5}));
  not not_1 (not_1_out, in_5);
  and and_1 (and_1_out, REMAINDER_div_zero_flag, in_5, OPERATION);
  and and_2 (and_2_out, not_1_out, OPERATION, MULTIPLICATION_f1);
  Decoder decoder_1 (
    .D(and_2_out), .C(multiplexer_2_out), .B(multiplexer_3_out), .A(multiplexer_1_out), .a_2(decoder_1_a_2),
    .b_2(decoder_1_b_2), .c_2(decoder_1_c_2), .d_2(decoder_1_d_2), .e(decoder_1_e), .f(decoder_1_f),
    .g(decoder_1_g));
  Multiplexer #(.select(2), .enable("false")) multiplexer_4 (
    .in0(ADDER___SUBTERACTOR_out_9), .in1(ADDER___SUBTERACTOR_out_9), .in2(MULTIPLICATION_sign_f),
    .in3(REMAINDER_sign_f), .out(multiplexer_4_out), .sel({OPERATION, in_5}));
  not not_2 (not_2_out, and_1_out);
  // Simple_buzzer simple_buzzer_1: pin names not known; wires that end beside it: and_1_out
  or or_1 (or_1_out, multiplexer_1_out, multiplexer_3_out, multiplexer_2_out, and_2_out);
  and and_3 (and_3_out, not_2_out, decoder_1_b_2);
  _7_Segment_Display u_7_segment_display_1 (
    .g(decoder_1_g), .f(decoder_1_f), .a(decoder_1_a_2), .b(and_3_out), .e(decoder_1_e), .d(decoder_1_d_2),
    .c(and_4_out));  // open: dp
  _7_Segment_Display u_7_segment_display_2 (.g(multiplexer_4_out));  // open: f, a, b, e, d, c, dp
  and and_4 (and_4_out, decoder_1_c_2, not_2_out);
  LED Zero_Flag (.in(not_3_out));
  not not_3 (not_3_out, or_1_out);

  // Notes on the sheet:
  //   Operation Codes:
  //   00 Addition
  //   01 Subtraction
  //   10 Multiplication
  //   11 Remainder
  //   Div/Zero Flag
endmodule

module Add___Sub (
  input  A_sign,
  input  A1,
  input  A0,
  input  OPERATION,
  input  in_5,
  input  B_sign,
  input  B1,
  input  B0,
  output out_9,
  output out_10,
  output out_11,
  output out_12
);

  wire adder_1_cout, adder_1_out, adder_2_cout, adder_2_out, adder_3_cout, adder_3_out,
       n2_s_comp_representation_1_b0, n2_s_comp_representation_1_b1, n2_s_comp_representation_1_b3,
       n2_s_comp_representation_2_b0, n2_s_comp_representation_2_b1, n2_s_comp_representation_2_b3,
       n2s_comp_1_b0, n2s_comp_1_b1, n2s_comp_1_b3, xor_1_out, xor_2_out, xor_3_out;

  _2_s_Comp__Representation u_2_s_comp_representation_1 (
    .A0(A0), .A1(A1), .A2_Sign(A_sign), .B0(n2_s_comp_representation_1_b0),
    .B1(n2_s_comp_representation_1_b1), .B3(n2_s_comp_representation_1_b3));
  _2_s_Comp__Representation u_2_s_comp_representation_2 (
    .A0(B0), .A1(B1), .A2_Sign(B_sign), .B0(n2_s_comp_representation_2_b0),
    .B1(n2_s_comp_representation_2_b1), .B3(n2_s_comp_representation_2_b3));
  xor xor_1 (xor_1_out, n2_s_comp_representation_2_b0, in_5);
  xor xor_2 (xor_2_out, n2_s_comp_representation_2_b1, in_5);
  xor xor_3 (xor_3_out, in_5, n2_s_comp_representation_2_b3);
  Adder #(.width(1)) adder_1 (
    .a(n2_s_comp_representation_1_b0), .b(xor_1_out), .out(adder_1_out), .cin(in_5), .cout(adder_1_cout));
  Adder #(.width(1)) adder_2 (
    .a(n2_s_comp_representation_1_b1), .b(xor_2_out), .out(adder_2_out), .cin(adder_1_cout),
    .cout(adder_2_cout));
  Adder #(.width(1)) adder_3 (
    .a(n2_s_comp_representation_1_b3), .b(xor_3_out), .out(adder_3_out), .cin(adder_2_cout),
    .cout(adder_3_cout));
  Adder #(.width(1)) adder_4 (
    .a(n2_s_comp_representation_1_b3), .b(xor_3_out), .out(out_9), .cin(adder_3_cout));  // open: cout
  _2s_Comp u_2s_comp_1 (
    .A2(adder_3_out), .A1(adder_2_out), .A0(adder_1_out), .B3(n2s_comp_1_b3), .B1(n2s_comp_1_b1),
    .B0(n2s_comp_1_b0));
  Multiplexer multiplexer_1 (.in0(adder_1_out), .in1(n2s_comp_1_b0), .out(out_12), .sel(out_9));  // open: en
  Multiplexer multiplexer_2 (.in0(adder_2_out), .in1(n2s_comp_1_b1), .out(out_11), .sel(out_9));  // open: en
  Multiplexer multiplexer_3 (.in0(adder_3_out), .in1(n2s_comp_1_b3), .out(out_10), .sel(out_9));  // open: en
endmodule

module Multiplication (
  input  Sign_B,
  input  B1,
  input  B0,
  input  Sign_A,
  input  B1_2,
  input  B0_2,
  output Sign_F,
  output F1,
  output F2,
  output F3,
  output F4
);

  wire adder_1_cout, and_1_out, and_2_out, and_3_out, or_1_out, xor_1_out;

  and and_1 (and_1_out, B1_2, B0);
  and and_2 (and_2_out, B1, B0_2);
  and and_3 (and_3_out, B1_2, B1);
  xor xor_1 (xor_1_out, Sign_B, Sign_A);
  and and_4 (F4, B0_2, B0);
  Adder #(.width(1)) adder_1 (.a(and_1_out), .b(and_2_out), .out(F3), .cout(adder_1_cout));  // open: cin
  Adder #(.width(1)) adder_2 (.a(adder_1_cout), .b(and_3_out), .out(F2), .cout(F1));  // open: cin
  or or_1 (or_1_out, F4, F3, F2, F1);
  and and_5 (Sign_F, or_1_out, xor_1_out);
endmodule

module Remainder (
  input  Sign_A,
  input  A0,
  input  A1,
  input  Sign_B,
  input  B0,
  input  B1,
  output Sign_F,
  output F0,
  output F1,
  output Div_Zero_Flag
);

  wire and_1_out, and_2_out, and_3_out, and_4_out, not_1_out, not_2_out, or_1_out, or_3_out;

  and and_1 (and_1_out, A1, B0);
  not not_1 (not_1_out, and_1_out);
  not not_2 (not_2_out, A0);
  and and_2 (and_2_out, not_2_out, A1);
  and and_3 (and_3_out, B0, B1);
  and and_4 (and_4_out, A0, B1, not_1_out);
  or or_1 (or_1_out, B0, B1);
  not not_3 (Div_Zero_Flag, or_1_out);
  and and_5 (F1, and_2_out, and_3_out);
  or or_2 (F0, and_4_out, Div_Zero_Flag);
  or or_3 (or_3_out, F1, and_4_out);
  and and_6 (Sign_F, or_3_out, Sign_A);

  // Notes on the sheet:
  //   Useless
endmodule

module _2s_Comp (
  input  A2,
  input  A1,
  input  A0,
  output B3,
  output B1,
  output B0
);

  wire or_1_out;

  or or_1 (or_1_out, A0, A1);
  xor xor_1 (B1, A0, A1);
  xor xor_2 (B3, or_1_out, A2);

  assign B0 = A0;
endmodule

module _2_s_Comp__Representation (
  input  A0,
  input  A1,
  input  A2_Sign,
  output B0,
  output B1,
  output B3
);

  wire or_1_out, xor_1_out;

  xor xor_1 (xor_1_out, A1, A0);
  Multiplexer multiplexer_1 (.in0(A1), .in1(xor_1_out), .out(B1), .sel(A2_Sign));  // open: en
  or or_1 (or_1_out, B1, A0);
  Multiplexer multiplexer_2 (.in0(A2_Sign), .in1(or_1_out), .out(B3), .sel(A2_Sign));  // open: en

  assign B0 = A0;

  // Notes on the sheet:
  //   Convert Signed Magnitude To 2's complement representation
endmodule

module Decoder (
  input  D,
  input  C,
  input  B,
  input  A,
  output a_2,
  output b_2,
  output c_2,
  output d_2,
  output e,
  output f,
  output g
);

  wire and_1_out, and_2_out, and_3_out, and_4_out, and_5_out, and_6_out, and_7_out, and_8_out, and_9_out,
       and_10_out, and_11_out, and_12_out, and_13_out, and_14_out, and_15_out, and_16_out, not_1_out,
       not_2_out, not_3_out, not_4_out, not_5_out, not_6_out, not_7_out, not_8_out, not_9_out, not_10_out,
       not_11_out, not_12_out, not_13_out, not_14_out, not_15_out, not_16_out, not_17_out, not_18_out,
       not_19_out, not_20_out, not_21_out;

  not not_1 (not_1_out, C);
  and and_1 (and_1_out, not_1_out, not_2_out);
  not not_2 (not_2_out, A);
  and and_2 (and_2_out, C, A);
  not not_3 (not_3_out, C);
  not not_4 (not_4_out, B);
  and and_3 (and_3_out, not_4_out, not_5_out);
  not not_5 (not_5_out, A);
  and and_4 (and_4_out, B, A);
  not not_6 (not_6_out, B);
  or or_1 (c_2, not_6_out, A, C);
  not not_7 (not_7_out, C);
  and and_5 (and_5_out, not_7_out, not_8_out);
  not not_8 (not_8_out, A);
  not not_9 (not_9_out, C);
  and and_6 (and_6_out, not_9_out, B);
  and and_7 (and_7_out, B, not_10_out);
  not not_10 (not_10_out, A);
  and and_8 (and_8_out, C, not_11_out, A);
  not not_11 (not_11_out, B);
  not not_12 (not_12_out, C);
  and and_9 (and_9_out, not_12_out, not_13_out);
  not not_13 (not_13_out, A);
  and and_10 (and_10_out, B, not_14_out);
  not not_14 (not_14_out, A);
  not not_15 (not_15_out, B);
  and and_11 (and_11_out, not_15_out, not_16_out);
  not not_16 (not_16_out, A);
  and and_12 (and_12_out, C, not_17_out);
  not not_17 (not_17_out, B);
  and and_13 (and_13_out, C, not_18_out);
  not not_18 (not_18_out, A);
  not not_19 (not_19_out, C);
  and and_14 (and_14_out, not_19_out, B);
  and and_15 (and_15_out, C, not_20_out);
  not not_20 (not_20_out, B);
  and and_16 (and_16_out, C, not_21_out);
  not not_21 (not_21_out, A);
  or or_2 (a_2, and_1_out, B, and_2_out, D);
  or or_3 (b_2, not_3_out, and_3_out, and_4_out);
  or or_4 (d_2, and_5_out, and_6_out, and_7_out, and_8_out, D);
  or or_5 (e, and_9_out, and_10_out);
  or or_6 (f, and_11_out, and_12_out, and_13_out, D);
  or or_7 (g, and_14_out, and_15_out, and_16_out, D);
endmodule
